// Logisim project design.circ as structural Verilog: 8 circuits, main circuit main
module main (
);

  wire alu_1_negative, alu_1_zero, branchcontrol_1_registersourcepcormux1, clock_1_out, control_1_alusrc,
       control_1_jpc, control_1_jump, control_1_memread, control_1_memtoreg, control_1_memwrite,
       control_1_regdst, control_1_regwrite, control_1_statusregwrite, or_1_out, statusregister_1_negative_2,
       statusregister_1_zero_2;
  wire [1:0] branchcontrol_1_addrdecision, control_1_branch;
  wire [2:0] alucontrol_1_operation, control_1_aluop;
  wire [4:0] multiplexer_1_out, multiplexer_2_out;
  wire [23:0] alu_1_result, shifter_1_out, shifter_3_out;
  wire [31:0] adder_1_out, adder_2_out, bit_extender_1_out, multiplexer_3_out, multiplexer_4_out,
       multiplexer_5_out, multiplexer_6_out, pc_1_out_4, ram_1_data, registerfile_1_outdata1,
       registerfile_1_outdata2, rom_1_data, shifter_2_out;
  wire [31:24] alu_1_result_2, shifter_1_out_2;

  Clock clock_1 (.out(clock_1_out));
  PC pc_1 (.Clock(clock_1_out), .PC(multiplexer_4_out), .out_4(pc_1_out_4));  // open: in_3
  Adder #(.width(32)) adder_1 (.a(32'h4), .b(pc_1_out_4), .out(adder_1_out));  // open: cin, cout
  Shifter #(.width(32), .shift("lr")) shifter_1 (
    .in(pc_1_out_4), .\dist (5'b00010), .out({shifter_1_out_2, shifter_1_out}));
  ROM #(.addrWidth(24), .dataWidth(32)) rom_1 (.addr(shifter_1_out), .data(rom_1_data));  // open: sel
  or or_1 (or_1_out, control_1_jump, control_1_jpc);
  Multiplexer #(.width(5), .enable("false")) multiplexer_1 (
    .in0(rom_1_data[20:16]), .in1(rom_1_data[15:11]), .out(multiplexer_1_out), .sel(control_1_regdst));
  Multiplexer #(.width(5), .enable("false")) multiplexer_2 (
    .in0(multiplexer_1_out), .in1(5'b01111), .out(multiplexer_2_out), .sel(or_1_out));
  Control control_1 (
    .OpCode(rom_1_data[31:26]), .RegDst(control_1_regdst), .AlUSrc(control_1_alusrc),
    .MemToReg(control_1_memtoreg), .RegWrite(control_1_regwrite), .MemWrite(control_1_memwrite),
    .AluOp(control_1_aluop), .Funct(rom_1_data[5:0]), .StatusRegWrite(control_1_statusregwrite),
    .MemRead(control_1_memread), .Jump(control_1_jump), .Jpc(control_1_jpc), .Branch(control_1_branch));
  RegisterFile registerfile_1 (
    .Load(control_1_regwrite), .InData(multiplexer_6_out), .Clk(clock_1_out), .WR(multiplexer_2_out),
    .outData1(registerfile_1_outdata1), .outData2(registerfile_1_outdata2), .rd2(rom_1_data[20:16]),
    .rd1(rom_1_data[25:21]));
  assign bit_extender_1_out = {{16{rom_1_data[15]}}, rom_1_data[15:0]};  // Bit_Extender bit_extender_1
  Multiplexer #(.width(32), .enable("false")) multiplexer_3 (
    .in0(registerfile_1_outdata2), .in1(bit_extender_1_out), .out(multiplexer_3_out), .sel(control_1_alusrc));
  Shifter #(.width(32)) shifter_2 (.in(bit_extender_1_out), .\dist (5'b00010), .out(shifter_2_out));
  AluControl alucontrol_1 (.AluOP(control_1_aluop), .\function (rom_1_data[5:0]), .Operation(alucontrol_1_operation));
  ALU alu_1 (
    .A(registerfile_1_outdata1), .B(multiplexer_3_out), .Gin(alucontrol_1_operation), .Zero(alu_1_zero),
    .Result({alu_1_result_2, alu_1_result}), .Negative(alu_1_negative), .Shamt(rom_1_data[10:6]));
  Adder #(.width(32)) adder_2 (.a(adder_1_out), .b(shifter_2_out), .out(adder_2_out));  // open: cin, cout
  StatusRegister statusregister_1 (
    .negative(alu_1_negative), .zero(alu_1_zero), .clk(clock_1_out), .zero_2(statusregister_1_zero_2),
    .negative_2(statusregister_1_negative_2), .load(control_1_statusregwrite));
  Shifter #(.width(24), .shift("lr")) shifter_3 (.in(alu_1_result), .\dist (5'b00010), .out(shifter_3_out));
  BranchControl branchcontrol_1 (
    .Jump(control_1_jump), .Branch(control_1_branch), .Negative(statusregister_1_negative_2),
    .Zero(statusregister_1_zero_2), .AddrDecision(branchcontrol_1_addrdecision), .Jpc(control_1_jpc),
    .RegisterSourcePcOrMux1(branchcontrol_1_registersourcepcormux1));
  Multiplexer #(.select(2), .width(32), .disabled(0), .enable("false")) multiplexer_4 (
    .in0(adder_1_out), .in1(ram_1_data), .in2(adder_2_out), .in3(registerfile_1_outdata2),
    .out(multiplexer_4_out), .sel(branchcontrol_1_addrdecision));
  RAM #(.addrWidth(24), .dataWidth(32), .bus("separate")) ram_1 (
    .addr(shifter_3_out), .din(registerfile_1_outdata2), .data(ram_1_data), .str(control_1_memwrite),
    .clk(clock_1_out), .ld(control_1_memread));  // open: sel, clr
  Multiplexer #(.width(32), .enable("false")) multiplexer_5 (
    .in0({alu_1_result_2, alu_1_result}), .in1(ram_1_data), .out(multiplexer_5_out), .sel(control_1_memtoreg));
  Multiplexer #(.width(32), .enable("false")) multiplexer_6 (
    .in0(adder_1_out), .in1(multiplexer_5_out), .out(multiplexer_6_out),
    .sel(branchcontrol_1_registersourcepcormux1));

  // Notes on the sheet:
  //   contents of rom_1 (hex, n*v repeats v):
  //   3421000a 34630001 211020 822020 431022 9c40fffd 852024 7800fffb
endmodule

module PC (
  input  [31:0] PC,
  input  Clock,
  input  in_3,
  output [31:0] out_4
);

  Register #(.width(32), .trigger("falling")) register_1 (.D(PC), .en(1'b1), .Q(out_4), .clk(Clock), .clr(in_3));
endmodule

module ALU (
  input  [31:0] A,
  input  [31:0] B,
  input  [2:0] Gin,
  input  [4:0] Shamt,
  output Negative,
  output Zero,
  output [31:0] Result
);

  wire [31:0] adder_1_out, and_1_out, bit_extender_1_out, or_1_out, shifter_1_out, subtractor_1_out;

  assign or_1_out = A | B;  // OR_Gate or_1, 32 bits wide
  assign and_1_out = A & B;  // AND_Gate and_1, 32 bits wide
  Adder #(.width(32)) adder_1 (.a(A), .b(B), .out(adder_1_out));  // open: cin, cout
  Subtractor #(.width(32)) subtractor_1 (.a(A), .b(B), .out(subtractor_1_out));  // open: bin, bout
  Shifter #(.width(32), .shift("lr")) shifter_1 (.in(B), .\dist (Shamt), .out(shifter_1_out));
  assign bit_extender_1_out = {{31{1'b0}}, subtractor_1_out[31]};  // Bit_Extender bit_extender_1
  Multiplexer #(.select(3), .width(32), .enable("false")) multiplexer_1 (
    .in0(and_1_out), .in1(or_1_out), .in2(adder_1_out), .in3(A), .in5(shifter_1_out), .in6(subtractor_1_out),
    .in7(bit_extender_1_out), .out({Negative, Result[30:0]}), .sel(Gin));  // open: in4
  Comparator #(.width(32), .mode("unsigned")) comparator_1 (
    .a({Negative, Result[30:0]}), .b({32{1'b0}}), .eq(Zero));  // open: gt, lt

  assign Result[31] = Negative;
endmodule

// Control Unit
module Control (
  input  [5:0] OpCode,
  input  [5:0] Funct,
  output Jpc,
  output RegDst,
  output AlUSrc,
  output MemToReg,
  output Jump,
  output RegWrite,
  output MemRead,
  output StatusRegWrite,
  output MemWrite,
  output [1:0] Branch,
  output [2:0] AluOp
);

  wire and_1_out, Balrn_out, Beq_out, Bgez_out, Jmadd_out, not_1_out, not_2_out, not_3_out, not_4_out,
       not_5_out, not_6_out, not_7_out, not_8_out, not_9_out, not_10_out, not_11_out, not_12_out, not_13_out,
       not_14_out, not_15_out, not_16_out, not_17_out, not_18_out, not_19_out, not_20_out, not_21_out,
       not_22_out, not_23_out, not_24_out, not_25_out, not_27_out, not_28_out, not_29_out, not_30_out;

  not not_1 (not_1_out, OpCode[1]);
  not not_2 (not_2_out, OpCode[5]);
  not not_3 (not_3_out, OpCode[2]);
  not not_4 (not_4_out, OpCode[0]);
  not not_5 (not_5_out, OpCode[4]);
  not not_6 (not_6_out, OpCode[3]);
  and R_Format (RegDst, not_2_out, not_5_out, not_6_out, not_3_out, not_1_out, not_4_out);
  not not_7 (not_7_out, OpCode[3]);
  not not_8 (not_8_out, OpCode[4]);
  not not_9 (not_9_out, OpCode[2]);
  and Lw (MemToReg, OpCode[5], not_8_out, not_7_out, not_9_out, OpCode[1], OpCode[0]);
  not not_10 (not_10_out, OpCode[2]);
  not not_11 (not_11_out, OpCode[4]);
  and Sw (MemWrite, OpCode[5], not_11_out, OpCode[3], not_10_out, OpCode[1], OpCode[0]);
  not not_12 (not_12_out, OpCode[5]);
  not not_13 (not_13_out, OpCode[3]);
  not not_14 (not_14_out, OpCode[4]);
  and Beq (Beq_out, not_12_out, not_14_out, not_13_out, OpCode[2], not_18_out, not_16_out);
  not not_15 (not_15_out, OpCode[5]);
  not not_16 (not_16_out, OpCode[0]);
  not not_17 (not_17_out, OpCode[4]);
  not not_18 (not_18_out, OpCode[1]);
  not not_19 (not_19_out, OpCode[1]);
  not not_20 (not_20_out, OpCode[4]);
  and Ori (AluOp[2], not_15_out, not_17_out, OpCode[3], OpCode[2], not_19_out, OpCode[0]);
  or or_1 (AlUSrc, MemToReg, AluOp[2], MemWrite);
  not not_21 (not_21_out, OpCode[3]);
  not not_22 (not_22_out, OpCode[5]);
  and Bgez (Bgez_out, OpCode[5], not_20_out, not_21_out, OpCode[2], OpCode[1], OpCode[0]);
  or or_2 (RegWrite, Jpc, RegDst, MemToReg, AluOp[2]);
  not not_23 (not_23_out, OpCode[0]);
  and u_Jpc (Jpc, not_22_out, OpCode[4], OpCode[3], OpCode[2], OpCode[1], not_23_out);
  or or_3 (AluOp[1], RegDst, Bgez_out);
  or or_4 (AluOp[0], Bgez_out, Beq_out);
  and and_1 (and_1_out, RegDst, Balrn_out);
  not not_24 (not_24_out, Funct[5]);
  or or_5 (Branch[1], and_1_out, Bgez_out);
  or or_6 (Branch[0], Beq_out, and_1_out);
  not not_25 (not_25_out, Funct[3]);
  and Balrn (Balrn_out, not_24_out, Funct[4], not_25_out, Funct[2], Funct[1], Funct[0]);
  not not_26 (StatusRegWrite, and_1_out);
  not not_27 (not_27_out, Funct[1]);
  not not_28 (not_28_out, Funct[2]);
  not not_29 (not_29_out, Funct[4]);
  not not_30 (not_30_out, Funct[3]);
  and Jmadd (Jmadd_out, Funct[5], not_29_out, not_30_out, not_28_out, not_27_out, Funct[0]);
  and and_2 (Jump, RegDst, Jmadd_out);
  or or_7 (MemRead, MemToReg, Jump);
endmodule

// ALUControl
module AluControl (
  input  [2:0] AluOP,
  input  [5:0] \function ,
  output [2:0] Operation
);

  wire and_2_out, and_3_out, and_4_out, and_5_out, not_1_out, not_2_out, not_4_out, not_5_out, not_6_out;
  wire [2:0] a0_out, or_1_out;

  not not_1 (not_1_out, AluOP[0]);
  not not_2 (not_2_out, AluOP[1]);
  not not_3 (or_1_out[1], AluOP[2]);
  not not_4 (not_4_out, \function [4]);
  not not_5 (not_5_out, \function [2]);
  not not_6 (not_6_out, \function [5]);
  and and_1 (or_1_out[2], AluOP[0], not_2_out);
  and and_2 (and_2_out, \function [1], not_4_out);
  or or_1 (or_1_out[0], AluOP[1], AluOP[2]);
  or a2 (a0_out[2], \function [3], and_2_out);
  and and_3 (and_3_out, \function [5], not_5_out);
  or a1 (a0_out[1], \function [3], \function [4], and_3_out);
  or a0 (a0_out[0], and_4_out, \function [3], not_6_out);
  and and_4 (and_4_out, \function [2], \function [0]);
  and and_5 (and_5_out, AluOP[1], not_1_out, or_1_out[1]);
  Multiplexer #(.width(3), .enable("false")) multiplexer_1 (
    .in0(or_1_out), .in1(a0_out), .out(Operation), .sel(and_5_out));
endmodule

// ST
module StatusRegister (
  input  negative,
  input  zero,
  input  load,
  input  clk,
  output zero_2,
  output negative_2
);

  Register #(.width(1)) register_1 (.D(zero), .en(load), .Q(zero_2), .clk(clk));  // open: clr
  Register #(.width(1)) register_2 (.D(negative), .en(load), .Q(negative_2), .clk(clk));  // open: clr
endmodule

module BranchControl (
  input  Jump,
  input  [1:0] Branch,
  input  Negative,
  input  Zero,
  input  Jpc,
  output [1:0] AddrDecision,
  output RegisterSourcePcOrMux1
);

  wire and_1_out, and_2_out, and_3_out, and_4_out, not_1_out, not_2_out, not_3_out, not_4_out, or_1_out;
  wire [1:0] b0_out;

  not not_1 (not_1_out, Branch[0]);
  not not_2 (not_2_out, Branch[1]);
  not not_3 (not_3_out, Negative);
  and and_1 (and_1_out, Branch[0], Branch[1], Negative);
  and and_2 (and_2_out, Zero, Branch[0], not_2_out);
  and and_3 (and_3_out, not_1_out, Branch[1], not_3_out);
  or or_1 (or_1_out, and_1_out, and_2_out, and_3_out);
  or b0 (b0_out[0], Jump, and_1_out);
  not not_4 (not_4_out, Jump);
  and b1 (b0_out[1], not_4_out, or_1_out);
  and and_4 (and_4_out, b0_out[0], b0_out[1]);
  Multiplexer #(.width(2), .disabled(0), .enable("false")) multiplexer_1 (
    .in0(b0_out), .in1(2'b10), .out(AddrDecision), .sel(Jpc));
  nor nor_1 (RegisterSourcePcOrMux1, Jump, and_4_out, Jpc);
endmodule

module RegisterFile (
  input  Load,
  input  [31:0] InData,
  input  Clk,
  input  [4:0] rd1,
  input  [4:0] WR,
  input  [4:0] rd2,
  output [31:0] outData1,
  output [31:0] outData2
);

  wire and_1_out, and_2_out, and_3_out, and_4_out, and_5_out, and_6_out, and_7_out, and_8_out, and_9_out,
       and_10_out, and_11_out, and_12_out, and_13_out, and_14_out, and_15_out, and_16_out, decoder_1_out0,
       decoder_1_out1, decoder_1_out2, decoder_1_out3, decoder_1_out4, decoder_1_out5, decoder_1_out6,
       decoder_1_out7, decoder_1_out8, decoder_1_out9, decoder_1_out10, decoder_1_out11, decoder_1_out12,
       decoder_1_out13, decoder_1_out14, decoder_1_out15;
  wire [31:0] R0, R1, R2, R3, R4, R5, R6, R7, R8, R9, R10, R11, R12, R13, R14, R15;

  Decoder #(.select(4), .enable("false")) decoder_1 (
    .out0(decoder_1_out0), .out1(decoder_1_out1), .out2(decoder_1_out2), .out3(decoder_1_out3),
    .out4(decoder_1_out4), .out5(decoder_1_out5), .out6(decoder_1_out6), .out7(decoder_1_out7),
    .out8(decoder_1_out8), .out9(decoder_1_out9), .out10(decoder_1_out10), .out11(decoder_1_out11),
    .out12(decoder_1_out12), .out13(decoder_1_out13), .out14(decoder_1_out14), .out15(decoder_1_out15),
    .sel(WR[3:0]));
  and and_1 (and_1_out, Load, decoder_1_out0);
  and and_2 (and_2_out, Load, decoder_1_out1);
  and and_3 (and_3_out, Load, decoder_1_out2);
  and and_4 (and_4_out, Load, decoder_1_out3);
  and and_5 (and_5_out, Load, decoder_1_out4);
  and and_6 (and_6_out, Load, decoder_1_out5);
  and and_7 (and_7_out, Load, decoder_1_out6);
  and and_8 (and_8_out, Load, decoder_1_out7);
  Register #(.width(32), .trigger("falling")) u_R0 (.D(InData), .en(and_1_out), .Q(R0), .clk(Clk), .clr(1'b0));
  Register #(.width(32), .trigger("falling")) u_R1 (.D(InData), .en(and_2_out), .Q(R1), .clk(Clk), .clr(1'b0));
  Register #(.width(32), .trigger("falling")) u_R2 (.D(InData), .en(and_3_out), .Q(R2), .clk(Clk), .clr(1'b0));
  Register #(.width(32), .trigger("falling")) u_R3 (.D(InData), .en(and_4_out), .Q(R3), .clk(Clk), .clr(1'b0));
  Register #(.width(32), .trigger("falling")) u_R4 (.D(InData), .en(and_5_out), .Q(R4), .clk(Clk), .clr(1'b0));
  Register #(.width(32), .trigger("falling")) u_R5 (.D(InData), .en(and_6_out), .Q(R5), .clk(Clk), .clr(1'b0));
  Register #(.width(32), .trigger("falling")) u_R6 (.D(InData), .en(and_7_out), .Q(R6), .clk(Clk), .clr(1'b0));
  Register #(.width(32), .trigger("falling")) u_R7 (.D(InData), .en(and_8_out), .Q(R7), .clk(Clk), .clr(1'b0));
  and and_9 (and_9_out, Load, decoder_1_out8);
  and and_10 (and_10_out, Load, decoder_1_out9);
  and and_11 (and_11_out, Load, decoder_1_out10);
  and and_12 (and_12_out, Load, decoder_1_out11);
  and and_13 (and_13_out, Load, decoder_1_out12);
  and and_14 (and_14_out, Load, decoder_1_out13);
  and and_15 (and_15_out, Load, decoder_1_out14);
  and and_16 (and_16_out, Load, decoder_1_out15);
  Register #(.width(32), .trigger("falling")) u_R8 (.D(InData), .en(and_9_out), .Q(R8), .clk(Clk), .clr(1'b0));
  Register #(.width(32), .trigger("falling")) u_R9 (.D(InData), .en(and_10_out), .Q(R9), .clk(Clk), .clr(1'b0));
  Register #(.width(32), .trigger("falling")) u_R10 (.D(InData), .en(and_11_out), .Q(R10), .clk(Clk), .clr(1'b0));
  Register #(.width(32), .trigger("falling")) u_R11 (.D(InData), .en(and_12_out), .Q(R11), .clk(Clk), .clr(1'b0));
  Register #(.width(32), .trigger("falling")) u_R12 (.D(InData), .en(and_13_out), .Q(R12), .clk(Clk), .clr(1'b0));
  Register #(.width(32), .trigger("falling")) u_R13 (.D(InData), .en(and_14_out), .Q(R13), .clk(Clk), .clr(1'b0));
  Register #(.width(32), .trigger("falling")) u_R14 (.D(InData), .en(and_15_out), .Q(R14), .clk(Clk), .clr(1'b0));
  Register #(.width(32), .trigger("falling")) u_R15 (.D(InData), .en(and_16_out), .Q(R15), .clk(Clk), .clr(1'b0));
  Multiplexer #(.select(4), .width(32), .enable("false")) multiplexer_1 (
    .in0(R0), .in1(R1), .in2(R2), .in3(R3), .in4(R4), .in5(R5), .in6(R6), .in7(R7), .in8(R8), .in9(R9),
    .in10(R10), .in11(R11), .in12(R12), .in13(R13), .in14(R14), .in15(R15), .out(outData1), .sel(rd1[3:0]));
  Multiplexer #(.select(4), .width(32), .enable("false")) multiplexer_2 (
    .in0(R0), .in1(R1), .in2(R2), .in3(R3), .in4(R4), .in5(R5), .in6(R6), .in7(R7), .in8(R8), .in9(R9),
    .in10(R10), .in11(R11), .in12(R12), .in13(R13), .in14(R14), .in15(R15), .out(outData2), .sel(rd2[3:0]));
endmodule
